# Fritzing sketch ArduinoDojoShield (saved by Fritzing 0.9.1b)
circuit board: 6.87464cm x 5.34949cm
breadboards: 1

parts:
  R1 = Rotary Potentiometer (Large) [maximum_resistance=10kΩ package=THT]
  R2 = Resistor [tolerance=±5% resistance=10k package=THT]
  R3 = Photocell (LDR) [package=THT]
  LED1 = RGB LED (com. cathode, rgb) [package="5 mm [THT]"]
  S1 = Pushbutton [package="[THT]"]
  S2 = Pushbutton [package="[THT]"]
  J1 = Basic Servo
  J3 = female pin header, 3 pins [form="♀ (female)"]
  7_Segment1 = 7 Segment Display
  C1 = Electrolytic Capacitor [capacitance=100µF voltage=16V package="100 mil [THT, electrolytic]"]
  C2 = Ceramic Capacitor [capacitance=100nF package="200 mil [THT, multilayer]"]
  J2 = Basic Servo
  U1 = 74HC595 SMD [package="SO16 [SMD]"]
  R6 = Resistor [tolerance=±5% resistance=330 package="0603 [SMD]"]
  R4 = Resistor [tolerance=±5% resistance=330 package="0603 [SMD]"]
  R5 = Resistor [tolerance=±5% resistance=330 package="0603 [SMD]"]
  R12 = Resistor [tolerance=±5% resistance=330 package=THT]
  R10 = Resistor [tolerance=±5% resistance=330 package=THT]
  R9 = Resistor [tolerance=±5% resistance=330 package=THT]
  R8 = Resistor [tolerance=±5% resistance=330 package=THT]
  R7 = Resistor [tolerance=±5% resistance=330 package=THT]
  R6_2 = Resistor [tolerance=±5% resistance=330 package="0603 [SMD]"]
  Part1 = Arduino Uno (Rev3)
  R11 = Resistor [tolerance=±5% resistance=330 package="0603 [SMD]"]
  R13 = Resistor [tolerance=±5% resistance=330 package="0603 [SMD]"]

nets:
  GND: R1.leg1, R3.pin_0, LED1.common_cathode, S1.Pin_3, S1.Pin_4, S2.Pin_3, S2.Pin_4, J1.gnd, J3.pin3, 7_Segment1.common_cathode, C1.-, C2.0, J2.gnd, U1.GND, U1.OE, Part1.GND
  N1: R1.wiper, Part1.A5/SCL
  5V: R1.leg2, R2.Pin_1, J1.vcc, C1.+, C2.1, J2.vcc, U1.MR, U1.VCC, Part1.5V
  N2: R2.Pin_0, R3.pin_1, Part1.A3
  N3: LED1.red_anode, R6.Pin_1
  N4: LED1.green_anode, R5.Pin_1
  N5: LED1.blue_anode, R4.Pin_1
  N6: S1.Pin_1, S1.Pin_2, Part1.D7
  N7: S2.Pin_1, S2.Pin_2, Part1.D8
  servo1: J1.pulse, Part1.D9_PWM
  N8: J3.pin1, Part1.D0/RX
  N9: J3.pin2, Part1.D1/TX
  N10: 7_Segment1.Segment_E, R10.Pin_1
  N11: 7_Segment1.Segment_D, R9.Pin_1
  N12: 7_Segment1.Segment_C, R8.Pin_1
  N13: 7_Segment1.Segment_DP, R13.Pin_1
  N14: 7_Segment1.Segment_B, R7.Pin_1
  N15: 7_Segment1.Segment_A, R6_2.Pin_1
  N16: 7_Segment1.Segment_F, R11.Pin_1
  N17: 7_Segment1.Segment_G, R12.Pin_1
  servo2: J2.pulse, Part1.D10_PWM/SS
  N18: U1.Q1, R7.Pin_0
  N19: U1.Q2, R8.Pin_0
  N20: U1.Q3, R9.Pin_0
  N21: U1.Q4, R10.Pin_0
  N22: U1.Q5, R11.Pin_0
  N23: U1.Q6, R12.Pin_0
  N24: U1.Q7, R13.Pin_0
  N25: U1.SH_CP, Part1.D11_PWM/MOSI
  N26: U1.ST_CP, Part1.D12/MISO
  N27: U1.DS, Part1.D13/SCK
  N28: U1.Q0, R6_2.Pin_0
  N29: R6.Pin_0, Part1.D6_PWM
  N30: R4.Pin_0, Part1.D3_PWM
  N31: R5.Pin_0, Part1.D5_PWM

notes:
  3x 330 Ω
  8x 330 Ω
  dojo shield rev 1.0
